// Logisim project workshop.circ as structural Verilog: 1 circuit, main circuit main
module main (
  input  [7:0] in,
  input  wrap_around,
  input  load,
  input  shift,
  input  right,
  output [7:0] out,
  output [7:0] left_shifted,
  output [7:0] right_shifted
);

  wire clock_1_out, not_1_out;
  wire [7:0] multiplexer_1_out, multiplexer_2_out, multiplexer_4_out;

  Multiplexer #(.width(8), .enable("false")) multiplexer_1 (
    .in0({out[7], left_shifted[7:1]}), .in1(in), .out(multiplexer_1_out), .sel(load));
  Multiplexer #(.width(8), .enable("false")) multiplexer_2 (
    .in0(multiplexer_1_out), .in1(multiplexer_4_out), .out(multiplexer_2_out), .sel(shift));
  Clock clock_1 (.out(clock_1_out));
  not not_1 (not_1_out, clock_1_out);
  D_Flip_Flop d_ff_1 (.clk(not_1_out), .D(multiplexer_2_out[0]), .Q(left_shifted[1]));  // open: Qn, preset, en, reset
  D_Flip_Flop d_ff_2 (.clk(not_1_out), .D(multiplexer_2_out[1]), .Q(left_shifted[2]));  // open: Qn, preset, en, reset
  D_Flip_Flop d_ff_3 (.clk(not_1_out), .D(multiplexer_2_out[2]), .Q(left_shifted[3]));  // open: Qn, preset, en, reset
  D_Flip_Flop d_ff_4 (.clk(not_1_out), .D(multiplexer_2_out[3]), .Q(left_shifted[4]));  // open: Qn, preset, en, reset
  D_Flip_Flop d_ff_5 (.clk(not_1_out), .D(multiplexer_2_out[4]), .Q(left_shifted[5]));  // open: Qn, preset, en, reset
  D_Flip_Flop d_ff_6 (.clk(not_1_out), .D(multiplexer_2_out[5]), .Q(left_shifted[6]));  // open: Qn, preset, en, reset
  D_Flip_Flop d_ff_7 (.clk(not_1_out), .D(multiplexer_2_out[6]), .Q(left_shifted[7]));  // open: Qn, preset, en, reset
  D_Flip_Flop d_ff_8 (.clk(not_1_out), .D(multiplexer_2_out[7]), .Q(out[7]));  // open: Qn, preset, en, reset
  Multiplexer #(.enable("false")) multiplexer_3 (.in0(1'b0), .in1(out[7]), .out(left_shifted[0]), .sel(wrap_around));
  Multiplexer #(.width(8), .enable("false")) multiplexer_4 (
    .in0(left_shifted), .in1({right_shifted[7], out[7], left_shifted[7:2]}), .out(multiplexer_4_out),
    .sel(right));
  Multiplexer #(.enable("false")) multiplexer_5 (
    .in0(1'b0), .in1(left_shifted[1]), .out(right_shifted[7]), .sel(wrap_around));

  assign out[6:0] = left_shifted[7:1];
  assign right_shifted[6:0] = {out[7], left_shifted[7:2]};
endmodule
