// Logisim project workshop.circ as structural Verilog: 1 circuit, main circuit main
module main (
  input  In,
  output Out
);

  wire and_1_out, and_2_out, and_3_out, and_4_out, and_5_out, clock_1_out, LSB_state__Sb_q, MSB_state__Sa_q,
       nor_1_out, not_1_out, not_2_out, not_3_out, or_1_out;

  not not_1 (not_1_out, MSB_state__Sa_q);
  and and_1 (and_1_out, not_1_out, LSB_state__Sb_q);
  not not_2 (not_2_out, In);
  not not_3 (not_3_out, LSB_state__Sb_q);
  and and_2 (and_2_out, and_1_out, In);
  and and_3 (and_3_out, not_2_out, and_4_out);
  and and_4 (and_4_out, MSB_state__Sa_q, not_3_out);
  Clock clock_1 (.out(clock_1_out));
  or or_1 (or_1_out, and_2_out, and_3_out);
  nor nor_1 (nor_1_out, In, LSB_state__Sb_q);
  D_Flip_Flop MSB_state__Sa (.clk(clock_1_out), .D(or_1_out), .Q(MSB_state__Sa_q));  // open: Qn, preset, en, reset
  and and_5 (and_5_out, MSB_state__Sa_q, In, LSB_state__Sb_q);
  D_Flip_Flop LSB_state__Sb (.clk(clock_1_out), .D(nor_1_out), .Q(LSB_state__Sb_q));  // open: Qn, preset, en, reset
  D_Flip_Flop Output (.clk(clock_1_out), .D(and_5_out), .Q(Out));  // open: Qn, preset, en, reset
endmodule
